// Logisim project displayde7segmentos.circ as structural Verilog: 1 circuit, main circuit main
module main (
  input  A,
  input  B,
  input  C,
  output out_4,
  output out_5,
  output out_6,
  output out_7,
  output out_8,
  output out_9,
  output out_10,
  output out_11
);

  wire A_out, B_out, C_out, D_out, E_out, F_out, G_out, not_1_out, not_2_out, not_3_out;

  not not_1 (not_1_out, B);
  not not_2 (not_2_out, A);
  not not_3 (not_3_out, C);
  and _07 (out_4, C, B, A);
  and _06 (out_5, not_3_out, B, A);
  and _05 (out_6, C, not_1_out, A);
  and _04 (out_7, not_3_out, not_1_out, A);
  and _03 (out_8, C, B, not_2_out);
  and _02 (out_9, not_3_out, B, not_2_out);
  and _01 (out_10, C, not_1_out, not_2_out);
  and _00 (out_11, not_3_out, not_1_out, not_2_out);
  or u_A (A_out, out_11, out_9, out_8, out_6, out_5, out_4);
  or u_B (B_out, out_11, out_10, out_9, out_8, out_7, out_4);
  or u_C (C_out, out_10, out_8, out_7, out_11, out_6, out_5, out_4);
  _7_Segment_Display u_7_segment_display_1 (
    .g(G_out), .f(F_out), .a(A_out), .b(B_out), .e(E_out), .d(D_out), .c(C_out));  // open: dp
  or D (D_out, out_11, out_8, out_6, out_5);
  or E (E_out, out_11, out_9, out_5);
  or F (F_out, out_11, out_7, out_6, out_5);
  or G (G_out, out_8, out_7, out_6, out_5);
endmodule
